# Fritzing sketch test_setup (saved by Fritzing 0.9.3b)
circuit board: 8.46667cm x 5.64444cm
breadboards: 1

parts:
  J1 = STM32 Nucleo boards
  R2 = Resistor [tolerance=±5% resistance=4.7k package=THT]
  IC1 = 24LC02 [package=THT]
  R1 = Resistor [tolerance=±5% resistance=4.7k package=THT]

nets:
  N1: J1.A4/SDA, R2.Pin_0, IC1.SDA_-_I2C_Data
  N2: J1.A5/SCL, IC1.SCL_-_I2C_Clock, R1.Pin_1
  N3: J1.3V3, R2.Pin_1, IC1.+V, R1.Pin_0
  N4: J1.GND, IC1.A0, IC1.A1, IC1.A2, IC1.0V, IC1.WP_-_Write_Protect
